# Fritzing sketch 01_LED (saved by Fritzing 0.9.3b)
breadboards: 1

parts:
  LED2 = LED - 3mm [color="Red (633nm)" package="3 mm [THT]"]
  R1 = Resistor [tolerance=±5% resistance=220 package=THT]
  S1 = Momentary Switch [package=ksa_sealed_tac_switch]
  Part1 = Arduino Uno (Rev3)

nets:
  N1: LED2.cathode, R1.Pin_0
  N2: LED2.anode, S1.2
  N3: R1.Pin_1, Part1.GND
  N4: S1.3, Part1.5V
