# Fritzing sketch 02_2LED (saved by Fritzing 0.9.3b)
breadboards: 1

parts:
  Part1 = Arduino Uno (Rev3)
  LED2 = LED - 3mm [color="Red (633nm)" package="3 mm [THT]"]
  R1 = Resistor [tolerance=±5% resistance=220 package=THT]
  LED4 = LED - 3mm [color="Red (633nm)" package="3 mm [THT]"]
  R2 = Resistor [tolerance=±5% resistance=220 package=THT]
  S1 = Momentary Switch [package=ksa_sealed_tac_switch]

nets:
  N1: Part1.D13/SCK, LED4.anode
  N2: Part1.5V, S1.3
  N3: Part1.GND, R1.Pin_1, R2.Pin_1
  N4: LED2.cathode, R1.Pin_0
  N5: LED2.anode, S1.2
  N6: LED4.cathode, R2.Pin_0
