# Fritzing sketch 03_BUTTON (saved by Fritzing 0.9.3b)
breadboards: 1

parts:
  Part1 = Arduino Uno (Rev3)
  LED4 = LED - 3mm [color="Red (633nm)" package="3 mm [THT]"]
  R2 = Resistor [tolerance=±5% resistance=220 package=THT]
  S1 = Momentary Switch [package=ksa_sealed_tac_switch]
  R3 = Resistor [tolerance=±5% resistance=10k package=THT]

nets:
  N1: Part1.D13/SCK, LED4.anode
  N2: Part1.D2, S1.2, R3.Pin_0
  N3: Part1.5V, S1.4
  N4: Part1.GND, R2.Pin_1, R3.Pin_1
  N5: LED4.cathode, R2.Pin_0
