# Fritzing sketch 04_POT (saved by Fritzing 0.9.3b)
breadboards: 1

parts:
  Part1 = Arduino Uno (Rev3)
  LED4 = LED - 3mm [color="Red (633nm)" package="3 mm [THT]"]
  R2 = Resistor [tolerance=±5% resistance=220 package=THT]
  R4 = Trimmer Potentiometer [maximum_resistance=10kΩ package=THT]

nets:
  N1: Part1.A5/SCL, R4.wiper
  N2: Part1.D13/SCK, LED4.anode
  N3: Part1.5V, R4.leg2
  N4: Part1.GND, R2.Pin_1, R4.leg1
  N5: LED4.cathode, R2.Pin_0
