# Fritzing sketch 04_POT_CAP (saved by Fritzing 0.9.3b)
breadboards: 1

parts:
  Part1 = Arduino Uno (Rev3)
  R4 = Trimmer Potentiometer [maximum_resistance=10kΩ package=THT]
  C1 = Electrolytic Capacitor [capacitance=0.1mF package="100 mil [THT, electrolytic]"]
  J1 = Basic Servo
  C2 = Electrolytic Capacitor [capacitance=0.1mF package="100 mil [THT, electrolytic]"]

nets:
  N1: Part1.A5/SCL, R4.wiper
  5V: Part1.5V, R4.leg2, C1.+, J1.vcc, C2.+
  GND: Part1.GND, R4.leg1, C1.-, J1.gnd, C2.-
