# Fritzing sketch 05_SERVO_no_cond (saved by Fritzing 0.9.2b)
breadboards: 1

parts:
  Part1 = Arduino Uno (Rev3)
  R4 = Trimmer Potentiometer [maximum_resistance=10kΩ package=THT]
  J1 = Basic Servo

nets:
  N1: Part1.A5/SCL, R4.wiper
  N2: Part1.D3_PWM, J1.pulse
  5V: Part1.5V, R4.leg2, J1.vcc
  GND: Part1.GND, R4.leg1, J1.gnd
