# Fritzing sketch 07_ULTIMATE (saved by Fritzing 0.9.2b)
breadboards: 1

parts:
  Part1 = Arduino Uno (Rev3)
  J1 = Basic Servo
  C2 = Electrolytic Capacitor [capacitance=0.1mF package="100 mil [THT, electrolytic]"]
  R1 = Resistor [tolerance=±5% resistance=220 package=THT]
  LED1 = smd LED [color="Red (633nm)" package="0603 [SMD]"]
  R2 = Resistor [tolerance=±5% resistance=10k package=THT]
  S1 = Pushbutton [package="[THT]"]

nets:
  N1: Part1.D2, LED1.anode
  N2: Part1.D3_PWM, J1.pulse
  N3: Part1.D7, R2.Pin_1, S1.Pin_3, S1.Pin_4
  5V: Part1.5V, J1.vcc, C2.+, S1.Pin_1, S1.Pin_2
  GND: Part1.GND, J1.gnd, C2.-, R1.Pin_0, R2.Pin_0
  N4: R1.Pin_1, LED1.cathode
